// Logisim project logisim_project.circ as structural Verilog: 1 circuit, main circuit 1bit ALU
module _1bit_ALU (
  input  Sub,
  input  Cin,
  input  [2:0] Sel,
  input  A,
  input  B,
  input  Less,
  input  Cout,
  input  Set,
  output Result
);

  wire and_1_out, nor_1_out, or_1_out, xor_1_out, xor_2_out;

  and and_1 (and_1_out, A, B);
  or or_1 (or_1_out, A, B);
  nor nor_1 (nor_1_out, A, B);
  xor xor_1 (xor_1_out, A, B);
  Adder #(.width(1)) adder_1 (.a(A), .b(xor_2_out), .out(Set), .cin(Cin), .cout(Cout));
  xor xor_2 (xor_2_out, B, Sub);
  Multiplexer #(.select(3), .enable("false")) multiplexer_1 (
    .in0(and_1_out), .in1(or_1_out), .in2(nor_1_out), .in3(xor_1_out), .in4(Set), .in5(Less), .out(Result),
    .sel(Sel));  // open: in6, in7
endmodule
